// Logisim project ula.circ as structural Verilog: 8 circuits, main circuit main
// S0
module main (
  output [7:0] out_1
);

  wire Clock_out, not_1_out, not_2_out, OverFlow_q, Reset_out, uc_1_clear_pc, uc_1_clk_ac, uc_1_clk_ir,
       uc_1_clk_pc, uc_1_clk_ram, uc_1_direcao, uc_1_load, uc_1_mod_end, uc_1_r_w, ula_1_ovfl, ula_1_zero,
       Zero_q;
  wire [2:0] uc_1_op_code;
  wire [3:0] AC_q, multiplexer_1_out, PC_q, ram_1_data, uc_1_endereco, uc_1_operando, ula_1_s;
  wire [7:0] rom_1_data;

  not not_1 (not_1_out, uc_1_load);
  ROM #(.addrWidth(4)) rom_1 (.addr(PC_q), .data(rom_1_data));  // open: sel
  Counter #(.width(4), .max('hf), .trigger("falling")) PC (
    .load(uc_1_load), .D(uc_1_endereco), .count(not_1_out), .Q(PC_q), .clk(uc_1_clk_pc), .clr(uc_1_clear_pc));  // open: carry
  Button Reset (.out(Reset_out));
  Clock Clock (.out(Clock_out));
  Register #(.trigger("high")) IR (.D(rom_1_data), .Q(out_1), .clk(uc_1_clk_ir));  // open: en, clr
  UC uc_1 (
    .Instrucao(out_1), .Operando(uc_1_operando), .Op_Code(uc_1_op_code), .CLK_PC(uc_1_clk_pc),
    .CLK_RAM(uc_1_clk_ram), .CLK_IR(uc_1_clk_ir), .CLK_AC(uc_1_clk_ac), .Reset(Reset_out), .Clock(Clock_out),
    .Clear_PC(uc_1_clear_pc), .Zero(Zero_q), .Carry(OverFlow_q), .Endereco(uc_1_endereco), .Load(uc_1_load),
    .R_W(uc_1_r_w), .Mod_End(uc_1_mod_end), .Direcao(uc_1_direcao));
  RAM #(.addrWidth(4), .dataWidth(4)) ram_1 (
    .addr(uc_1_operando), .data(ram_1_data), .clk(uc_1_clk_ram), .ld(uc_1_r_w));  // open: sel, clr
  Multiplexer #(.width(4), .enable("false")) multiplexer_1 (
    .in0(uc_1_operando), .in1(ram_1_data), .out(multiplexer_1_out), .sel(uc_1_mod_end));
  ULA ula_1 (
    .A(AC_q), .B(multiplexer_1_out), .\Operação (uc_1_op_code), .S(ula_1_s), .OVFL(ula_1_ovfl),
    .Zero(ula_1_zero), .in_1(uc_1_direcao));
  Register #(.width(4)) AC (.D(ula_1_s), .Q(AC_q), .clk(uc_1_clk_ac));  // open: en, clr
  assign ram_1_data = not_2_out ? AC_q : 4'bz;  // Controlled_Buffer controlled_buffer_1
  not not_2 (not_2_out, uc_1_r_w);
  D_Flip_Flop Zero (.clk(uc_1_clk_ac), .D(ula_1_zero), .Q(Zero_q));  // open: Qn, preset, en, reset
  D_Flip_Flop OverFlow (.clk(uc_1_clk_ac), .D(ula_1_ovfl), .Q(OverFlow_q));  // open: Qn, preset, en, reset

  // Notes on the sheet:
  //   contents of rom_1 (hex, n*v repeats v):
  //   0 f0 1 f1 10 31 d0 f2 11 f0 12 f1 e4
endmodule

module dec_2x4 (
  input  A,
  input  B,
  output S0,
  output S1,
  output S2,
  output S3
);

  and and_1 (S0, ~A, ~B);  // AND_Gate
  and and_2 (S1, ~A, B);  // AND_Gate
  and and_3 (S2, A, ~B);  // AND_Gate
  and and_4 (S3, A, B);
endmodule

module dec_3x8 (
  input  [2:0] Entrada,
  output S0,
  output S1,
  output S2,
  output S3,
  output S4,
  output S5,
  output S6,
  output S7
);

  wire not_1_out, not_2_out, not_3_out, not_4_out, not_5_out, not_6_out, not_7_out, not_8_out, not_9_out,
       not_10_out, not_11_out, not_12_out;

  not not_1 (not_1_out, Entrada[2]);
  not not_2 (not_2_out, Entrada[1]);
  and and_1 (S0, not_1_out, not_2_out, not_3_out);
  not not_3 (not_3_out, Entrada[0]);
  not not_4 (not_4_out, Entrada[2]);
  and and_2 (S1, not_4_out, not_5_out, Entrada[0]);
  not not_5 (not_5_out, Entrada[1]);
  not not_6 (not_6_out, Entrada[2]);
  and and_3 (S2, not_6_out, Entrada[1], not_7_out);
  not not_7 (not_7_out, Entrada[0]);
  not not_8 (not_8_out, Entrada[2]);
  and and_4 (S3, not_8_out, Entrada[1], Entrada[0]);
  not not_9 (not_9_out, Entrada[1]);
  and and_5 (S4, Entrada[2], not_9_out, not_10_out);
  not not_10 (not_10_out, Entrada[0]);
  and and_6 (S5, Entrada[2], not_11_out, Entrada[0]);
  not not_11 (not_11_out, Entrada[1]);
  and and_7 (S6, Entrada[2], Entrada[1], not_12_out);
  not not_12 (not_12_out, Entrada[0]);
  and and_8 (S7, Entrada[2], Entrada[1], Entrada[0]);
endmodule

module Soma (
  input  A,
  input  B,
  input  Vem1,
  output S,
  output Vai1
);

  wire and_1_out, and_2_out, and_3_out, xor_1_out;

  xor xor_1 (xor_1_out, A, Vem1);
  and and_1 (and_1_out, A, Vem1);
  and and_2 (and_2_out, A, B);
  and and_3 (and_3_out, Vem1, B);
  xor xor_2 (S, B, xor_1_out);
  or or_1 (Vai1, and_1_out, and_2_out, and_3_out);
endmodule

module Soma_4 (
  input  [3:0] B,
  input  [3:0] A,
  input  in_3,
  output OVF,
  output [3:0] Resultado
);

  wire soma_1_vai1, soma_3_vai1, soma_4_vai1;

  Soma soma_1 (.S(Resultado[2]), .Vai1(soma_1_vai1), .A(B[2]), .B(A[2]), .Vem1(soma_3_vai1));
  Soma soma_2 (.S(Resultado[3]), .Vai1(OVF), .A(B[3]), .B(A[3]), .Vem1(soma_1_vai1));
  Soma soma_3 (.S(Resultado[1]), .Vai1(soma_3_vai1), .A(B[1]), .B(A[1]), .Vem1(soma_4_vai1));
  Soma soma_4 (.S(Resultado[0]), .Vai1(soma_4_vai1), .A(B[0]), .B(A[0]), .Vem1(in_3));
endmodule

module Ou_4bits (
  input  [3:0] A,
  input  [3:0] B,
  output [3:0] S
);

  or or_1 (S[3], A[3], B[3]);
  or or_2 (S[2], A[2], B[2]);
  or or_3 (S[0], A[0], B[0]);
  or or_4 (S[1], A[1], B[1]);
endmodule

module ULA (
  input  in_1,
  input  [3:0] A,
  input  [3:0] B,
  input  [2:0] \Operação ,
  output [3:0] S,
  output OVFL,
  output Zero
);

  wire and_1_out, and_2_out, dec_3x8_1_s0, dec_3x8_1_s1, dec_3x8_1_s2, dec_3x8_1_s3, dec_3x8_1_s4,
       dec_3x8_1_s5, dec_3x8_1_s6, dec_3x8_1_s7, not_1_out, soma_4_1_ovf, subtractor_1_bout;
  wire [3:0] controlled_buffer_6_out, ou_4bits_1_s, shifter_1_out, shifter_2_out, soma_4_1_resultado,
       subtractor_1_out;

  dec_3x8 dec_3x8_1 (
    .S0(dec_3x8_1_s0), .S1(dec_3x8_1_s1), .S2(dec_3x8_1_s2), .S3(dec_3x8_1_s3), .S4(dec_3x8_1_s4),
    .S5(dec_3x8_1_s5), .S6(dec_3x8_1_s6), .S7(dec_3x8_1_s7), .Entrada(\Operação ));
  assign S = dec_3x8_1_s0 ? B : 4'bz;  // Controlled_Buffer controlled_buffer_1
  nor nor_1 (Zero, dec_3x8_1_s7, dec_3x8_1_s6, S[0], S[1], S[2], S[3]);
  and and_1 (and_1_out, dec_3x8_1_s1, soma_4_1_ovf);
  Soma_4 soma_4_1 (.A(A), .OVF(soma_4_1_ovf), .B(B), .in_3(1'b0), .Resultado(soma_4_1_resultado));
  assign S = dec_3x8_1_s1 ? soma_4_1_resultado : 4'bz;  // Controlled_Buffer controlled_buffer_2
  or or_1 (OVFL, and_1_out, and_2_out);
  Subtractor #(.width(4)) subtractor_1 (.a(A), .b(B), .out(subtractor_1_out), .bout(subtractor_1_bout));  // open: bin
  assign S = dec_3x8_1_s3 ? subtractor_1_out : 4'bz;  // Controlled_Buffer controlled_buffer_3
  and and_2 (and_2_out, dec_3x8_1_s3, subtractor_1_bout);
  Ou_4bits ou_4bits_1 (.S(ou_4bits_1_s), .A(B), .B(A));
  assign S = dec_3x8_1_s2 ? ou_4bits_1_s : 4'bz;  // Controlled_Buffer controlled_buffer_4
  assign S = dec_3x8_1_s4 ? ~B : 4'bz;  // Controlled_Inverter controlled_inverter_1
  assign S = dec_3x8_1_s5 ? controlled_buffer_6_out : 4'bz;  // Controlled_Buffer controlled_buffer_5
  assign controlled_buffer_6_out = in_1 ? shifter_1_out : 4'bz;  // Controlled_Buffer controlled_buffer_6
  Shifter #(.width(4), .shift("lr")) shifter_1 (.in(A), .\dist (B[1:0]), .out(shifter_1_out));
  not not_1 (not_1_out, in_1);
  Shifter #(.width(4)) shifter_2 (.in(A), .\dist (B[1:0]), .out(shifter_2_out));
  assign controlled_buffer_6_out = not_1_out ? shifter_2_out : 4'bz;  // Controlled_Buffer controlled_buffer_7
endmodule

module UC (
  input  [7:0] Instrucao,
  input  Clock,
  input  Reset,
  input  Carry,
  input  Zero,
  output CLK_IR,
  output CLK_RAM,
  output Clear_PC,
  output CLK_AC,
  output CLK_PC,
  output Mod_End,
  output Direcao,
  output [3:0] Endereco,
  output [3:0] Operando,
  output [2:0] Op_Code,
  output R_W,
  output Load
);

  wire and_5_out, GoTo_out, JC_out, JZ_out;
  wire [1:0] counter_1_q;

  nand Store (R_W, CLK_AC, Instrucao[7], Instrucao[6], Instrucao[5], Instrucao[4]);
  Counter #(.width(2), .max('h3)) counter_1 (.Q(counter_1_q), .clk(Clock), .clr(Reset));  // open: load, D, count, carry
  and and_1 (CLK_IR, ~counter_1_q[1], ~counter_1_q[0]);  // AND_Gate
  and and_2 (CLK_PC, ~counter_1_q[1], counter_1_q[0]);  // AND_Gate
  and and_3 (CLK_AC, counter_1_q[1], ~counter_1_q[0]);  // AND_Gate
  and GoTo (GoTo_out, CLK_PC, Instrucao[7], Instrucao[6], Instrucao[5], ~Instrucao[4]);  // AND_Gate
  and and_4 (CLK_RAM, counter_1_q[1], counter_1_q[0]);
  and JC (JC_out, CLK_PC, Instrucao[7], Instrucao[6], ~Instrucao[5], Instrucao[4], Carry);  // AND_Gate
  or or_1 (Load, GoTo_out, JC_out, JZ_out);
  and JZ (JZ_out, CLK_PC, Instrucao[7], Instrucao[6], ~Instrucao[5], ~Instrucao[4], Zero);  // AND_Gate
  and and_5 (and_5_out, Instrucao[7], ~Instrucao[6], Instrucao[5]);  // AND_Gate
  and and_6 (Mod_End, ~and_5_out, Instrucao[4]);  // AND_Gate

  assign Clear_PC = Reset;
  assign Direcao = Instrucao[4];
  assign Endereco = Instrucao[3:0];
  assign Op_Code = Instrucao[7:5];
  assign Operando = Instrucao[3:0];
endmodule
